# Fritzing sketch mobbob-fritzing (saved by Fritzing 0.9.3b)
breadboards: 1

parts:
  Arduino_uno = Arduino Uno (Rev3) - ICSP
  Cadera_der = Dagu DGServo 9g (Top view) [part_number=RS001B]
  Pie_izq = Dagu DGServo 9g (Top view) [part_number=RS001B]
  Cadera_izq = Dagu DGServo 9g (Top view) [part_number=RS001B]
  Pie_der = Dagu DGServo 9g (Top view) [part_number=RS001B]
  HC-06 = Bluetooth HC-05 Macho
  Bateria_5V = 4 x AAA Battery Mount

nets:
  GND: Arduino_uno.GND, Cadera_der.gnd, Pie_izq.gnd, Cadera_izq.gnd, Pie_der.gnd, HC-06.GND, Bateria_5V.-
  N1: Arduino_uno.D10_PWM/SS, HC-06.TXD
  N2: Arduino_uno.D11_PWM/MOSI, HC-06.RXD
  N3: Arduino_uno.D2, Pie_izq.pulse
  N4: Arduino_uno.D3_PWM, Cadera_der.pulse
  N5: Arduino_uno.D4, Pie_der.pulse
  N6: Arduino_uno.D5_PWM, Cadera_izq.pulse
  5V: Arduino_uno.5V, HC-06.VCC
  VCC: Cadera_der.vcc, Pie_izq.vcc, Cadera_izq.vcc, Pie_der.vcc, Bateria_5V.+
